# Fritzing sketch leds_iot (saved by Fritzing 0.9.3b)
breadboards: 1

parts:
  Raspberry_Pi_1 = Raspberry Pi 3 [part_number=RPI-3-V1.2]
  LED1 = smd LED [color="Green (555nm)" package="0805 [SMD]"]
  LED2 = smd LED [color="Red (633nm)" package="0805 [SMD]"]
  R2 = Resistor [tolerance=±5% resistance=330 package=THT]
  R1 = Resistor [tolerance=±5% resistance=330 package=THT]

nets:
  N1: Raspberry_Pi_1.GND, R2.Pin_1, R1.Pin_1
  N2: Raspberry_Pi_1.GIPO17, LED2.anode
  N3: Raspberry_Pi_1.GIPO18, LED1.anode
  N4: LED1.cathode, R2.Pin_0
  N5: LED2.cathode, R1.Pin_0

notes:
  led pwm
  led ON/OFF
